// Digital circuit RISC16x.dig as structural Verilog
module RISC16x (
  input  [15:0] in_2,
  input  [15:0] in_3,
  input  in_4,
  input  in_5,
  input  in_6,
  input  in_7,
  input  in_8,
  output [15:0] out_1
);

  wire _74typeflipflop_1_always, _74typeflipflop_1_loaded_a, _74typeflipflop_1_loaded_b,
       _74typeflipflop_2_always, _74typeflipflop_2_loaded_a, _74typeflipflop_2_loaded_b,
       _74typeflipflop_3_always, _74typeflipflop_3_loaded_a, _74typeflipflop_3_loaded_b,
       _74typeflipflop_4_always, _74typeflipflop_4_loaded_a, _74typeflipflop_4_loaded_b,
       _74typeflipflop_5_always, _74typeflipflop_5_loaded_a, _74typeflipflop_5_loaded_b,
       _74typeflipflop_6_always, _74typeflipflop_6_loaded_a, _74typeflipflop_6_loaded_b,
       _74typeflipflop_7_always, _74typeflipflop_7_loaded_a, _74typeflipflop_7_loaded_b,
       _74typeflipflop_8_always, _74typeflipflop_8_loaded_a, _74typeflipflop_8_loaded_b, and_1_out,
       and_2_out, and_3_out, and_4_out, and_5_out, and_6_out, and_7_out, and_8_out, and_9_out, and_10_out,
       and_11_out, and_12_out, and_13_out, and_14_out, and_15_out, and_16_out, and_17_out, and_18_out,
       and_19_out, and_20_out, and_21_out, and_22_out, and_23_out, and_24_out, and_25_out, and_26_out,
       and_27_out, and_28_out, and_29_out, and_30_out, and_31_out, and_32_out, and_33_out, and_34_out,
       and_35_out, and_36_out, and_37_out, and_38_out, and_39_out, and_40_out, and_41_out, and_42_out,
       and_43_out, and_44_out, and_45_out, and_46_out, and_47_out, and_48_out, and_49_out, and_50_out,
       and_51_out, and_52_out, and_53_out, and_54_out, and_55_out, and_56_out, and_57_out, and_58_out,
       and_59_out, and_60_out, and_61_out, and_62_out, and_63_out, and_64_out, and_65_out, and_66_out,
       and_67_out, and_68_out, and_69_out, and_70_out, and_71_out, and_72_out, and_73_out, and_74_out,
       and_75_out, and_76_out, and_77_out, and_78_out, and_79_out, and_80_out, and_81_out, and_82_out,
       and_83_out, and_84_out, and_85_out, and_86_out, and_87_out, and_88_out, and_89_out, and_90_out,
       and_91_out, and_92_out, and_93_out, and_94_out, and_95_out, and_96_out, and_97_out, and_98_out,
       and_99_out, and_100_out, and_101_out, and_102_out, and_103_out, and_104_out, and_106_out, and_107_out,
       and_108_out, and_109_out, and_110_out, and_111_out, and_112_out, and_113_out, and_114_out,
       and_115_out, and_116_out, and_117_out, and_118_out, and_119_out, and_120_out, and_121_out,
       and_122_out, and_123_out, and_124_out, and_125_out, and_126_out, and_127_out, and_128_out,
       and_129_out, and_130_out, and_131_out, and_132_out, and_133_out, and_134_out, and_135_out,
       and_136_out, and_137_out, and_138_out, and_139_out, and_140_out, and_141_out, and_142_out,
       and_143_out, and_144_out, and_145_out, and_146_out, and_147_out, and_148_out, and_149_out,
       and_150_out, and_151_out, and_152_out, and_153_out, and_154_out, and_155_out, and_156_out,
       and_157_out, and_158_out, and_159_out, and_160_out, and_161_out, and_162_out, and_163_out,
       and_164_out, and_165_out, and_166_out, and_167_out, and_168_out, and_169_out, and_170_out,
       and_171_out, and_172_out, and_173_out, and_174_out, and_175_out, and_176_out, and_177_out,
       and_178_out, and_179_out, and_180_out, and_181_out, and_182_out, and_183_out, and_184_out,
       and_185_out, and_186_out, and_187_out, and_188_out, and_189_out, and_190_out, and_191_out,
       and_192_out, and_193_out, and_194_out, and_195_out, and_196_out, and_197_out, and_198_out,
       and_199_out, and_200_out, and_201_out, and_202_out, and_203_out, and_204_out, and_205_out,
       and_206_out, and_207_out, and_208_out, and_209_out, and_210_out, dipswitch_1_out, not_1_out,
       not_2_out, not_3_out, not_4_out, not_5_out, not_6_out, not_7_out, not_8_out, not_9_out, not_10_out,
       not_11_out, not_12_out, not_13_out, not_14_out, not_15_out, not_16_out, not_17_out, not_18_out,
       not_19_out, not_20_out, not_21_out, not_22_out, not_23_out, not_24_out, not_25_out, or_1_out,
       or_2_out, or_3_out, or_4_out, or_5_out, or_6_out, or_7_out, or_8_out, or_9_out, or_10_out, or_11_out,
       or_12_out, or_13_out, or_14_out, or_15_out, or_16_out, or_17_out, or_18_out, or_19_out, or_20_out,
       or_21_out, or_22_out, or_23_out, or_24_out, or_25_out, or_26_out, or_27_out, or_28_out, or_29_out,
       or_30_out, or_31_out, or_32_out, or_33_out, or_34_out, or_35_out, or_36_out, or_37_out, or_38_out,
       or_39_out, or_40_out, or_41_out, or_42_out, undriven, undriven_2, undriven_3, undriven_4, undriven_5,
       undriven_6, undriven_7, undriven_8, undriven_9, undriven_10, undriven_11, undriven_12, xor_1_out,
       xor_2_out, xor_3_out, xor_4_out, xor_5_out, xor_6_out, xor_7_out, xor_8_out, xor_9_out, xor_10_out,
       xor_11_out, xor_12_out, xor_13_out, xor_14_out, xor_15_out, xor_16_out, xor_17_out, xor_18_out,
       xor_19_out, xor_20_out, xor_21_out, xor_22_out, xor_23_out, xor_24_out, xor_25_out, xor_26_out,
       xor_27_out, xor_28_out, xor_29_out, xor_30_out, xor_31_out, xor_32_out;
  wire [7:0] xor_56_out, xor_64_out;
  wire [15:0] notconnected_1_out;

  DipSwitch dipswitch_1 (.out(dipswitch_1_out));
  xor xor_1 (xor_1_out, in_2[15], dipswitch_1_out);
  xor xor_2 (xor_2_out, in_2[14], dipswitch_1_out);
  xor xor_3 (xor_3_out, in_2[13], dipswitch_1_out);
  xor xor_4 (xor_4_out, dipswitch_1_out, in_2[12]);
  xor xor_5 (xor_5_out, dipswitch_1_out, in_2[11]);
  xor xor_6 (xor_6_out, dipswitch_1_out, in_2[10]);
  xor xor_7 (xor_7_out, dipswitch_1_out, in_2[9]);
  xor xor_8 (xor_8_out, dipswitch_1_out, in_2[8]);
  xor xor_9 (xor_9_out, in_2[7], dipswitch_1_out);
  xor xor_10 (xor_10_out, in_2[6], dipswitch_1_out);
  xor xor_11 (xor_11_out, in_2[5], dipswitch_1_out);
  xor xor_12 (xor_12_out, dipswitch_1_out, in_2[4]);
  xor xor_13 (xor_13_out, dipswitch_1_out, in_2[3]);
  xor xor_14 (xor_14_out, dipswitch_1_out, in_2[2]);
  xor xor_15 (xor_15_out, dipswitch_1_out, in_2[1]);
  xor xor_16 (xor_16_out, dipswitch_1_out, in_2[0]);
  and and_1 (and_1_out, xor_1_out, in_3[15]);
  xor xor_17 (xor_17_out, xor_1_out, in_3[15]);
  and and_2 (and_2_out, xor_2_out, in_3[14]);
  xor xor_18 (xor_18_out, xor_2_out, in_3[14]);
  and and_3 (and_3_out, xor_3_out, in_3[13]);
  xor xor_19 (xor_19_out, xor_3_out, in_3[13]);
  and and_4 (and_4_out, xor_4_out, in_3[12]);
  xor xor_20 (xor_20_out, xor_4_out, in_3[12]);
  and and_5 (and_5_out, xor_5_out, in_3[11]);
  xor xor_21 (xor_21_out, xor_5_out, in_3[11]);
  and and_6 (and_6_out, xor_6_out, in_3[10]);
  xor xor_22 (xor_22_out, xor_6_out, in_3[10]);
  and and_7 (and_7_out, xor_7_out, in_3[9]);
  xor xor_23 (xor_23_out, xor_7_out, in_3[9]);
  and and_8 (and_8_out, xor_8_out, in_3[8]);
  xor xor_24 (xor_24_out, xor_8_out, in_3[8]);
  and and_9 (and_9_out, xor_9_out, in_3[7]);
  xor xor_25 (xor_25_out, xor_9_out, in_3[7]);
  and and_10 (and_10_out, xor_10_out, in_3[6]);
  xor xor_26 (xor_26_out, xor_10_out, in_3[6]);
  and and_11 (and_11_out, xor_11_out, in_3[5]);
  xor xor_27 (xor_27_out, xor_11_out, in_3[5]);
  and and_12 (and_12_out, xor_12_out, in_3[4]);
  xor xor_28 (xor_28_out, xor_12_out, in_3[4]);
  and and_13 (and_13_out, xor_13_out, in_3[3]);
  xor xor_29 (xor_29_out, xor_13_out, in_3[3]);
  and and_14 (and_14_out, xor_14_out, in_3[2]);
  xor xor_30 (xor_30_out, xor_14_out, in_3[2]);
  and and_15 (and_15_out, xor_15_out, in_3[1]);
  xor xor_31 (xor_31_out, xor_15_out, in_3[1]);
  and and_16 (and_16_out, xor_16_out, in_3[0]);
  xor xor_32 (xor_32_out, xor_16_out, in_3[0]);
  and and_17 (and_17_out, or_19_out, xor_20_out);
  and and_18 (and_18_out, xor_19_out, xor_18_out);
  and and_19 (and_19_out, and_4_out, xor_19_out);
  and and_20 (and_20_out, xor_18_out, xor_17_out);
  and and_21 (and_21_out, xor_17_out, xor_18_out);
  and and_22 (and_22_out, and_2_out, xor_17_out);
  and and_23 (and_23_out, xor_18_out, xor_19_out);
  and and_24 (and_24_out, xor_20_out, or_19_out);
  and and_25 (and_25_out, xor_19_out, xor_18_out);
  and and_26 (and_26_out, and_3_out, xor_18_out);
  and and_27 (and_27_out, xor_20_out, xor_19_out);
  and and_28 (and_28_out, xor_19_out, and_4_out);
  and and_29 (and_29_out, xor_20_out, or_19_out);
  and and_30 (and_30_out, or_21_out, xor_24_out);
  and and_31 (and_31_out, xor_23_out, xor_22_out);
  and and_32 (and_32_out, and_8_out, xor_23_out);
  and and_33 (and_33_out, xor_22_out, xor_21_out);
  and and_34 (and_34_out, xor_21_out, xor_22_out);
  and and_35 (and_35_out, and_6_out, xor_21_out);
  and and_36 (and_36_out, xor_22_out, xor_23_out);
  and and_37 (and_37_out, xor_24_out, or_21_out);
  and and_38 (and_38_out, xor_23_out, xor_22_out);
  and and_39 (and_39_out, and_7_out, xor_22_out);
  and and_40 (and_40_out, xor_24_out, xor_23_out);
  and and_41 (and_41_out, xor_23_out, and_8_out);
  and and_42 (and_42_out, xor_24_out, or_21_out);
  and and_43 (and_43_out, or_23_out, xor_28_out);
  and and_44 (and_44_out, xor_27_out, xor_26_out);
  and and_45 (and_45_out, and_12_out, xor_27_out);
  and and_46 (and_46_out, xor_26_out, xor_25_out);
  and and_47 (and_47_out, xor_25_out, xor_26_out);
  and and_48 (and_48_out, and_10_out, xor_25_out);
  and and_49 (and_49_out, xor_26_out, xor_27_out);
  and and_50 (and_50_out, xor_28_out, or_23_out);
  and and_51 (and_51_out, xor_27_out, xor_26_out);
  and and_52 (and_52_out, and_11_out, xor_26_out);
  and and_53 (and_53_out, xor_28_out, xor_27_out);
  and and_54 (and_54_out, xor_27_out, and_12_out);
  and and_55 (and_55_out, xor_28_out, or_23_out);
  and and_56 (and_56_out, dipswitch_1_out, xor_32_out);
  and and_57 (and_57_out, xor_31_out, xor_30_out);
  and and_58 (and_58_out, and_16_out, xor_31_out);
  and and_59 (and_59_out, xor_30_out, xor_29_out);
  and and_60 (and_60_out, xor_29_out, xor_30_out);
  and and_61 (and_61_out, and_14_out, xor_29_out);
  and and_62 (and_62_out, xor_30_out, xor_31_out);
  and and_63 (and_63_out, xor_32_out, dipswitch_1_out);
  and and_64 (and_64_out, xor_31_out, xor_30_out);
  and and_65 (and_65_out, and_15_out, xor_30_out);
  and and_66 (and_66_out, xor_32_out, xor_31_out);
  and and_67 (and_67_out, xor_31_out, and_16_out);
  and and_68 (and_68_out, xor_32_out, dipswitch_1_out);
  and and_69 (and_69_out, and_17_out, and_18_out);
  and and_70 (and_70_out, and_19_out, and_20_out);
  and and_71 (and_71_out, and_21_out, and_3_out);
  and and_72 (and_72_out, and_23_out, and_24_out);
  and and_73 (and_73_out, and_25_out, and_4_out);
  and and_74 (and_74_out, and_27_out, or_19_out);
  or or_1 (or_1_out, and_29_out, and_4_out);
  and and_75 (and_75_out, and_30_out, and_31_out);
  and and_76 (and_76_out, and_32_out, and_33_out);
  and and_77 (and_77_out, and_34_out, and_7_out);
  and and_78 (and_78_out, and_36_out, and_37_out);
  and and_79 (and_79_out, and_38_out, and_8_out);
  and and_80 (and_80_out, and_40_out, or_21_out);
  or or_2 (or_2_out, and_42_out, and_8_out);
  and and_81 (and_81_out, and_43_out, and_44_out);
  and and_82 (and_82_out, and_45_out, and_46_out);
  and and_83 (and_83_out, and_47_out, and_11_out);
  and and_84 (and_84_out, and_49_out, and_50_out);
  and and_85 (and_85_out, and_51_out, and_12_out);
  and and_86 (and_86_out, and_53_out, or_23_out);
  or or_3 (or_3_out, and_55_out, and_12_out);
  and and_87 (and_87_out, and_56_out, and_57_out);
  and and_88 (and_88_out, and_58_out, and_59_out);
  and and_89 (and_89_out, and_60_out, and_15_out);
  and and_90 (and_90_out, and_62_out, and_63_out);
  and and_91 (and_91_out, and_64_out, and_16_out);
  and and_92 (and_92_out, and_66_out, dipswitch_1_out);
  or or_4 (or_4_out, and_68_out, and_16_out);
  and and_93 (and_93_out, and_69_out, xor_17_out);
  and and_94 (and_94_out, and_75_out, xor_21_out);
  and and_95 (and_95_out, and_81_out, xor_25_out);
  and and_96 (and_96_out, and_87_out, xor_29_out);
  or or_5 (or_5_out, and_72_out, and_73_out);
  or or_6 (or_6_out, and_26_out, and_2_out);
  or or_7 (or_7_out, and_74_out, and_28_out);
  or or_8 (or_8_out, and_78_out, and_79_out);
  or or_9 (or_9_out, and_39_out, and_6_out);
  or or_10 (or_10_out, and_80_out, and_41_out);
  or or_11 (or_11_out, and_84_out, and_85_out);
  or or_12 (or_12_out, and_52_out, and_10_out);
  or or_13 (or_13_out, and_86_out, and_54_out);
  or or_14 (or_14_out, and_90_out, and_91_out);
  or or_15 (or_15_out, and_65_out, and_14_out);
  or or_16 (or_16_out, and_92_out, and_67_out);
  or or_17 (or_17_out, or_26_out, and_1_out);
  or or_18 (or_18_out, or_7_out, and_3_out);
  or or_19 (or_19_out, or_29_out, and_5_out);
  or or_20 (or_20_out, or_10_out, and_7_out);
  or or_21 (or_21_out, or_32_out, and_9_out);
  or or_22 (or_22_out, or_13_out, and_11_out);
  or or_23 (or_23_out, or_35_out, and_13_out);
  or or_24 (or_24_out, or_16_out, and_15_out);
  or or_25 (or_25_out, and_71_out, and_22_out);
  or or_26 (or_26_out, or_37_out, or_25_out);
  or or_27 (or_27_out, or_5_out, or_6_out);
  or or_28 (or_28_out, and_77_out, and_35_out);
  or or_29 (or_29_out, or_38_out, or_28_out);
  or or_30 (or_30_out, or_8_out, or_9_out);
  or or_31 (or_31_out, and_83_out, and_48_out);
  or or_32 (or_32_out, or_39_out, or_31_out);
  or or_33 (or_33_out, or_11_out, or_12_out);
  or or_34 (or_34_out, and_89_out, and_61_out);
  or or_35 (or_35_out, or_40_out, or_34_out);
  or or_36 (or_36_out, or_14_out, or_15_out);
  or or_37 (or_37_out, and_93_out, and_70_out);
  xor xor_33 (out_1[15], xor_17_out, or_27_out);
  xor xor_34 (out_1[14], xor_18_out, or_18_out);
  xor xor_35 (out_1[13], xor_19_out, or_1_out);
  xor xor_36 (out_1[12], or_19_out, xor_20_out);
  or or_38 (or_38_out, and_94_out, and_76_out);
  xor xor_37 (out_1[11], xor_21_out, or_30_out);
  xor xor_38 (out_1[10], xor_22_out, or_20_out);
  xor xor_39 (out_1[9], xor_23_out, or_2_out);
  xor xor_40 (out_1[8], or_21_out, xor_24_out);
  or or_39 (or_39_out, and_95_out, and_82_out);
  xor xor_41 (out_1[7], xor_25_out, or_33_out);
  xor xor_42 (out_1[6], xor_26_out, or_22_out);
  xor xor_43 (out_1[5], xor_27_out, or_3_out);
  xor xor_44 (out_1[4], or_23_out, xor_28_out);
  or or_40 (or_40_out, and_96_out, and_88_out);
  xor xor_45 (out_1[3], xor_29_out, or_36_out);
  xor xor_46 (out_1[2], xor_30_out, or_24_out);
  xor xor_47 (out_1[1], xor_31_out, or_4_out);
  xor xor_48 (out_1[0], dipswitch_1_out, xor_32_out);
  _74TypeFlipFlop _74typeflipflop_1 (
    .CLK(undriven_9), .Data(undriven_2), .Load_A(undriven_10), .Load_B(undriven_11),
    .Always(_74typeflipflop_1_always), .Loaded_A(_74typeflipflop_1_loaded_a),
    .Loaded_B(_74typeflipflop_1_loaded_b), .Reset(undriven_12));
  _74TypeFlipFlop _74typeflipflop_2 (
    .CLK(undriven_9), .Data(undriven_3), .Load_A(undriven_10), .Load_B(undriven_11),
    .Always(_74typeflipflop_2_always), .Loaded_A(_74typeflipflop_2_loaded_a),
    .Loaded_B(_74typeflipflop_2_loaded_b), .Reset(undriven_12));
  _74TypeFlipFlop _74typeflipflop_3 (
    .CLK(undriven_9), .Data(undriven_4), .Load_A(undriven_10), .Load_B(undriven_11),
    .Always(_74typeflipflop_3_always), .Loaded_A(_74typeflipflop_3_loaded_a),
    .Loaded_B(_74typeflipflop_3_loaded_b), .Reset(undriven_12));
  _74TypeFlipFlop _74typeflipflop_4 (
    .CLK(undriven_9), .Data(undriven_5), .Load_A(undriven_10), .Load_B(undriven_11),
    .Always(_74typeflipflop_4_always), .Loaded_A(_74typeflipflop_4_loaded_a),
    .Loaded_B(_74typeflipflop_4_loaded_b), .Reset(undriven_12));
  _74TypeFlipFlop _74typeflipflop_5 (
    .CLK(undriven_9), .Data(undriven_6), .Load_A(undriven_10), .Load_B(undriven_11),
    .Always(_74typeflipflop_5_always), .Loaded_A(_74typeflipflop_5_loaded_a),
    .Loaded_B(_74typeflipflop_5_loaded_b), .Reset(undriven_12));
  _74TypeFlipFlop _74typeflipflop_6 (
    .CLK(undriven_9), .Data(undriven_7), .Load_A(undriven_10), .Load_B(undriven_11),
    .Always(_74typeflipflop_6_always), .Loaded_A(_74typeflipflop_6_loaded_a),
    .Loaded_B(_74typeflipflop_6_loaded_b), .Reset(undriven_12));
  _74TypeFlipFlop _74typeflipflop_7 (
    .CLK(undriven_9), .Data(undriven_8), .Load_A(undriven_10), .Load_B(undriven_11),
    .Always(_74typeflipflop_7_always), .Loaded_A(_74typeflipflop_7_loaded_a),
    .Loaded_B(_74typeflipflop_7_loaded_b), .Reset(undriven_12));
  _74TypeFlipFlop _74typeflipflop_8 (
    .CLK(undriven_9), .Data(undriven), .Load_A(undriven_10), .Load_B(undriven_11),
    .Always(_74typeflipflop_8_always), .Loaded_A(_74typeflipflop_8_loaded_a),
    .Loaded_B(_74typeflipflop_8_loaded_b), .Reset(undriven_12));
  // NotConnected on notconnected_1_out
  and and_97 (and_97_out, and_98_out, notconnected_1_out[7]);
  xor xor_49 (xor_56_out[7], notconnected_1_out[7], and_98_out);
  and and_98 (and_98_out, and_99_out, notconnected_1_out[6]);
  xor xor_50 (xor_56_out[6], notconnected_1_out[6], and_99_out);
  and and_99 (and_99_out, and_100_out, notconnected_1_out[5]);
  xor xor_51 (xor_56_out[5], notconnected_1_out[5], and_100_out);
  and and_100 (and_100_out, and_101_out, notconnected_1_out[4]);
  xor xor_52 (xor_56_out[4], notconnected_1_out[4], and_101_out);
  and and_101 (and_101_out, and_102_out, notconnected_1_out[3]);
  xor xor_53 (xor_56_out[3], notconnected_1_out[3], and_102_out);
  and and_102 (and_102_out, and_103_out, notconnected_1_out[2]);
  xor xor_54 (xor_56_out[2], notconnected_1_out[2], and_103_out);
  and and_103 (and_103_out, and_104_out, notconnected_1_out[1]);
  xor xor_55 (xor_56_out[1], notconnected_1_out[1], and_104_out);
  and and_104 (and_104_out, 1'b1, notconnected_1_out[0]);
  xor xor_56 (xor_56_out[0], notconnected_1_out[0], 1'b1);
  // And and_105 has open pins: In_1=and_106_out, In_2=notconnected_1_out[15], out=open
  xor xor_57 (xor_64_out[7], notconnected_1_out[15], and_106_out);
  and and_106 (and_106_out, and_107_out, notconnected_1_out[14]);
  xor xor_58 (xor_64_out[6], notconnected_1_out[14], and_107_out);
  and and_107 (and_107_out, and_108_out, notconnected_1_out[13]);
  xor xor_59 (xor_64_out[5], notconnected_1_out[13], and_108_out);
  and and_108 (and_108_out, and_109_out, notconnected_1_out[12]);
  xor xor_60 (xor_64_out[4], notconnected_1_out[12], and_109_out);
  and and_109 (and_109_out, and_110_out, notconnected_1_out[11]);
  xor xor_61 (xor_64_out[3], notconnected_1_out[11], and_110_out);
  and and_110 (and_110_out, and_111_out, notconnected_1_out[10]);
  xor xor_62 (xor_64_out[2], notconnected_1_out[10], and_111_out);
  and and_111 (and_111_out, and_112_out, notconnected_1_out[9]);
  xor xor_63 (xor_64_out[1], notconnected_1_out[9], and_112_out);
  and and_112 (and_112_out, and_97_out, notconnected_1_out[8]);
  xor xor_64 (xor_64_out[0], notconnected_1_out[8], and_97_out);
  not not_1 (not_1_out, in_8);
  or or_41 (or_41_out, in_7, in_8);
  not not_2 (not_2_out, in_8);
  and and_113 (and_113_out, or_41_out, not_2_out);
  or or_42 (or_42_out, in_7, not_1_out);
  not not_3 (not_3_out, not_1_out);
  and and_114 (and_114_out, or_42_out, not_3_out);
  not not_4 (not_4_out, in_4);
  not not_5 (not_5_out, in_5);
  not not_6 (not_6_out, in_4);
  not not_7 (not_7_out, in_5);
  not not_8 (not_8_out, in_4);
  not not_9 (not_9_out, in_5);
  not not_10 (not_10_out, in_4);
  not not_11 (not_11_out, in_5);
  not not_12 (not_12_out, in_4);
  not not_13 (not_13_out, in_5);
  not not_14 (not_14_out, in_4);
  not not_15 (not_15_out, in_5);
  not not_16 (not_16_out, in_4);
  not not_17 (not_17_out, in_5);
  not not_18 (not_18_out, in_4);
  not not_19 (not_19_out, in_5);
  and and_115 (and_115_out, not_4_out, not_5_out);
  and and_116 (and_116_out, in_4, not_5_out);
  and and_117 (and_117_out, not_4_out, in_5);
  and and_118 (and_118_out, in_5, in_4);
  not not_20 (not_20_out, in_6);
  and and_119 (and_119_out, not_6_out, not_7_out);
  and and_120 (and_120_out, in_4, not_7_out);
  and and_121 (and_121_out, not_6_out, in_5);
  and and_122 (and_122_out, in_5, in_4);
  not not_21 (not_21_out, or_41_out);
  and and_123 (and_123_out, not_8_out, not_9_out);
  and and_124 (and_124_out, in_4, not_9_out);
  and and_125 (and_125_out, not_8_out, in_5);
  and and_126 (and_126_out, in_5, in_4);
  not not_22 (not_22_out, in_6);
  and and_127 (and_127_out, not_10_out, not_11_out);
  and and_128 (and_128_out, in_4, not_11_out);
  and and_129 (and_129_out, not_10_out, in_5);
  and and_130 (and_130_out, in_5, in_4);
  and and_131 (and_131_out, not_12_out, not_13_out);
  and and_132 (and_132_out, in_4, not_13_out);
  and and_133 (and_133_out, not_12_out, in_5);
  and and_134 (and_134_out, in_5, in_4);
  not not_23 (not_23_out, in_6);
  and and_135 (and_135_out, not_14_out, not_15_out);
  and and_136 (and_136_out, in_4, not_15_out);
  and and_137 (and_137_out, not_14_out, in_5);
  and and_138 (and_138_out, in_5, in_4);
  not not_24 (not_24_out, or_42_out);
  and and_139 (and_139_out, not_16_out, not_17_out);
  and and_140 (and_140_out, in_4, not_17_out);
  and and_141 (and_141_out, not_16_out, in_5);
  and and_142 (and_142_out, in_5, in_4);
  not not_25 (not_25_out, in_6);
  and and_143 (and_143_out, not_18_out, not_19_out);
  and and_144 (and_144_out, in_4, not_19_out);
  and and_145 (and_145_out, not_18_out, in_5);
  and and_146 (and_146_out, in_5, in_4);
  and and_147 (and_147_out, and_115_out, not_20_out);
  and and_148 (and_148_out, and_116_out, not_20_out);
  and and_149 (and_149_out, and_117_out, not_20_out);
  and and_150 (and_150_out, and_118_out, not_20_out);
  and and_151 (and_151_out, and_119_out, in_6);
  and and_152 (and_152_out, and_120_out, in_6);
  and and_153 (and_153_out, and_121_out, in_6);
  and and_154 (and_154_out, and_122_out, in_6);
  and and_155 (and_155_out, and_123_out, not_22_out);
  and and_156 (and_156_out, and_124_out, not_22_out);
  and and_157 (and_157_out, and_125_out, not_22_out);
  and and_158 (and_158_out, and_126_out, not_22_out);
  and and_159 (and_159_out, and_127_out, in_6);
  and and_160 (and_160_out, and_128_out, in_6);
  and and_161 (and_161_out, and_129_out, in_6);
  and and_162 (and_162_out, and_130_out, in_6);
  and and_163 (and_163_out, and_131_out, not_23_out);
  and and_164 (and_164_out, and_132_out, not_23_out);
  and and_165 (and_165_out, and_133_out, not_23_out);
  and and_166 (and_166_out, and_134_out, not_23_out);
  and and_167 (and_167_out, and_135_out, in_6);
  and and_168 (and_168_out, and_136_out, in_6);
  and and_169 (and_169_out, and_137_out, in_6);
  and and_170 (and_170_out, and_138_out, in_6);
  and and_171 (and_171_out, and_139_out, not_25_out);
  and and_172 (and_172_out, and_140_out, not_25_out);
  and and_173 (and_173_out, and_141_out, not_25_out);
  and and_174 (and_174_out, and_142_out, not_25_out);
  and and_175 (and_175_out, and_143_out, in_6);
  and and_176 (and_176_out, and_144_out, in_6);
  and and_177 (and_177_out, and_145_out, in_6);
  and and_178 (and_178_out, and_146_out, in_6);
  and and_179 (and_179_out, not_21_out, and_147_out);
  and and_180 (and_180_out, not_21_out, and_148_out);
  and and_181 (and_181_out, not_21_out, and_149_out);
  and and_182 (and_182_out, not_21_out, and_150_out);
  and and_183 (and_183_out, not_21_out, and_151_out);
  and and_184 (and_184_out, not_21_out, and_152_out);
  and and_185 (and_185_out, not_21_out, and_153_out);
  and and_186 (and_186_out, not_21_out, and_154_out);
  and and_187 (and_187_out, and_113_out, and_155_out);
  and and_188 (and_188_out, and_113_out, and_156_out);
  and and_189 (and_189_out, and_113_out, and_157_out);
  and and_190 (and_190_out, and_113_out, and_158_out);
  and and_191 (and_191_out, and_113_out, and_159_out);
  and and_192 (and_192_out, and_113_out, and_160_out);
  and and_193 (and_193_out, and_113_out, and_161_out);
  and and_194 (and_194_out, and_113_out, and_162_out);
  and and_195 (and_195_out, not_24_out, and_163_out);
  and and_196 (and_196_out, not_24_out, and_164_out);
  and and_197 (and_197_out, not_24_out, and_165_out);
  and and_198 (and_198_out, not_24_out, and_166_out);
  and and_199 (and_199_out, not_24_out, and_167_out);
  and and_200 (and_200_out, not_24_out, and_168_out);
  and and_201 (and_201_out, not_24_out, and_169_out);
  and and_202 (and_202_out, not_24_out, and_170_out);
  and and_203 (and_203_out, and_114_out, and_171_out);
  and and_204 (and_204_out, and_114_out, and_172_out);
  and and_205 (and_205_out, and_114_out, and_173_out);
  and and_206 (and_206_out, and_114_out, and_174_out);
  and and_207 (and_207_out, and_114_out, and_175_out);
  and and_208 (and_208_out, and_114_out, and_176_out);
  and and_209 (and_209_out, and_114_out, and_177_out);
  and and_210 (and_210_out, and_114_out, and_178_out);

  // Notes on the sheet:
  //   B
  //   A
  //   Generate
  //   Propogate
  //   C_0
  //   G_0
  //   P_3
  //   G_3
  //   P_2
  //   G_2
  //   P_1
  //   G_1
  //   P_0
  //   4-bit Carry Look-ahead
  //   5Inp
  //   4Inp
  //   3Inp
  //   .
  //   C_1
  //   C_4
  //   C_3
  //   C_2
  //   Clock
  //   Load_A
  //   Load_B
  //   Reset
  //   Register
  //   Data
  //   INCRMNT
  //   A_1
  //   A_2
  //   A_3
  //   A_4
  //   A_5
  //   5x32 Mux
  //   4x16 Mux
  //   A1
  //   A2
  //   A3
  //   A4
  //   Dis
  //   3x8 Mux
  //   Disable
  //   A_0
  //   2x4 Mux
endmodule
